// Digital circuit 2Way_Counter.dig as structural Verilog
module _2Way_Counter (
  input  clk,
  input  in_3,
  output [1:0] out_2
);

  wire and_1_out, and_2_out, and_3_out, and_4_out, d_ff_1_nq, d_ff_2_nq, not_1_out, or_1_out;

  not not_1 (not_1_out, in_3);
  and and_1 (and_1_out, not_1_out, d_ff_1_nq, d_ff_2_nq);
  and and_2 (and_2_out, in_3, d_ff_1_nq, out_2[0]);
  and and_3 (and_3_out, not_1_out, out_2[1], out_2[0]);
  and and_4 (and_4_out, in_3, out_2[1], d_ff_2_nq);
  or or_1 (or_1_out, and_1_out, and_2_out, and_3_out, and_4_out);
  D_FF d_ff_1 (.D(or_1_out), .C(clk), .Q(out_2[1]), .nQ(d_ff_1_nq));
  D_FF d_ff_2 (.D(d_ff_2_nq), .C(clk), .Q(out_2[0]), .nQ(d_ff_2_nq));
endmodule
