// Digital circuit 4-bit-processor.dig as structural Verilog
module _4_bit_processor (
  input  Clock,
  input  [1:0] InstructionMemory_ctrl,
  input  [1:0] InstructionPointer_ctrl,
  input  [3:0] InstructionMemory_dataInput,
  output [3:0] Output
);

  wire [3:0] Instruction_Memory_data_output, Program_Counter_output;

  Program_Counter_register Program_Counter (
    .Clock(Clock), .Input(4'b0000), .CLear_Store_Load_Increment(InstructionPointer_ctrl),
    .Increment_Value(4'b0001), .Output(Program_Counter_output));
  DRAM Instruction_Memory (
    .Clock(Clock), .Adress_Bus(Program_Counter_output), .Control_Bus(InstructionMemory_ctrl),
    .Data_Bus(InstructionMemory_dataInput), .Data_Output(Instruction_Memory_data_output));
  Instruction_Register Instruction_Register (
    .Clock(Clock), .Input(Instruction_Memory_data_output), .CLear_Store_Load(2'b01), .Output(Output));

  // Notes on the sheet:
  //   InstructionPointer_ctrl: default 3
endmodule
