// Digital circuit DRAM.dig as structural Verilog
module DRAM (
  input  Clock,
  input  [3:0] Adress_Bus,
  input  [1:0] Control_Bus,
  input  [3:0] Data_Bus,
  output [3:0] Data_Output
);

  wire and_1_out, and_2_out, and_3_out, and_4_out, and_5_out, and_6_out, and_7_out, and_8_out, and_9_out,
       and_10_out, and_11_out, and_12_out, and_13_out, and_14_out, and_15_out, and_16_out, decoder_1_out_0,
       decoder_1_out_1, decoder_1_out_2, decoder_1_out_3, decoder_1_out_4, decoder_1_out_5, decoder_1_out_6,
       decoder_1_out_7, decoder_1_out_8, decoder_1_out_9, decoder_1_out_10, decoder_1_out_11,
       decoder_1_out_12, decoder_1_out_13, decoder_1_out_14, decoder_1_out_15;
  wire [3:0] general_purpose_register_1_output, general_purpose_register_2_output,
       general_purpose_register_3_output, general_purpose_register_4_output,
       general_purpose_register_5_output, general_purpose_register_6_output,
       general_purpose_register_7_output, general_purpose_register_8_output,
       general_purpose_register_9_output, general_purpose_register_10_output,
       general_purpose_register_11_output, general_purpose_register_12_output,
       general_purpose_register_13_output, general_purpose_register_14_output,
       general_purpose_register_15_output, general_purpose_register_16_output;

  Decoder #(.Selector_Bits(4)) decoder_1 (
    .sel(Adress_Bus), .out_0(decoder_1_out_0), .out_1(decoder_1_out_1), .out_2(decoder_1_out_2),
    .out_3(decoder_1_out_3), .out_4(decoder_1_out_4), .out_5(decoder_1_out_5), .out_6(decoder_1_out_6),
    .out_7(decoder_1_out_7), .out_8(decoder_1_out_8), .out_9(decoder_1_out_9), .out_10(decoder_1_out_10),
    .out_11(decoder_1_out_11), .out_12(decoder_1_out_12), .out_13(decoder_1_out_13),
    .out_14(decoder_1_out_14), .out_15(decoder_1_out_15));
  and and_1 (and_1_out, decoder_1_out_0, Clock);
  and and_2 (and_2_out, decoder_1_out_4, Clock);
  and and_3 (and_3_out, decoder_1_out_8, Clock);
  and and_4 (and_4_out, decoder_1_out_12, Clock);
  General_Purpose_Register general_purpose_register_1 (
    .Clock(and_1_out), .Input(Data_Bus), .CLear_Store_Load(Control_Bus),
    .Output(general_purpose_register_1_output));
  General_Purpose_Register general_purpose_register_2 (
    .Clock(and_2_out), .Input(Data_Bus), .CLear_Store_Load(Control_Bus),
    .Output(general_purpose_register_2_output));
  General_Purpose_Register general_purpose_register_3 (
    .Clock(and_3_out), .Input(Data_Bus), .CLear_Store_Load(Control_Bus),
    .Output(general_purpose_register_3_output));
  General_Purpose_Register general_purpose_register_4 (
    .Clock(and_4_out), .Input(Data_Bus), .CLear_Store_Load(Control_Bus),
    .Output(general_purpose_register_4_output));
  and and_5 (and_5_out, decoder_1_out_1, Clock);
  and and_6 (and_6_out, decoder_1_out_5, Clock);
  and and_7 (and_7_out, decoder_1_out_9, Clock);
  and and_8 (and_8_out, decoder_1_out_13, Clock);
  General_Purpose_Register general_purpose_register_5 (
    .Clock(and_5_out), .Input(Data_Bus), .CLear_Store_Load(Control_Bus),
    .Output(general_purpose_register_5_output));
  General_Purpose_Register general_purpose_register_6 (
    .Clock(and_6_out), .Input(Data_Bus), .CLear_Store_Load(Control_Bus),
    .Output(general_purpose_register_6_output));
  General_Purpose_Register general_purpose_register_7 (
    .Clock(and_7_out), .Input(Data_Bus), .CLear_Store_Load(Control_Bus),
    .Output(general_purpose_register_7_output));
  General_Purpose_Register general_purpose_register_8 (
    .Clock(and_8_out), .Input(Data_Bus), .CLear_Store_Load(Control_Bus),
    .Output(general_purpose_register_8_output));
  and and_9 (and_9_out, decoder_1_out_2, Clock);
  and and_10 (and_10_out, decoder_1_out_6, Clock);
  and and_11 (and_11_out, decoder_1_out_10, Clock);
  and and_12 (and_12_out, decoder_1_out_14, Clock);
  General_Purpose_Register general_purpose_register_9 (
    .Clock(and_9_out), .Input(Data_Bus), .CLear_Store_Load(Control_Bus),
    .Output(general_purpose_register_9_output));
  General_Purpose_Register general_purpose_register_10 (
    .Clock(and_10_out), .Input(Data_Bus), .CLear_Store_Load(Control_Bus),
    .Output(general_purpose_register_10_output));
  General_Purpose_Register general_purpose_register_11 (
    .Clock(and_11_out), .Input(Data_Bus), .CLear_Store_Load(Control_Bus),
    .Output(general_purpose_register_11_output));
  General_Purpose_Register general_purpose_register_12 (
    .Clock(and_12_out), .Input(Data_Bus), .CLear_Store_Load(Control_Bus),
    .Output(general_purpose_register_12_output));
  and and_13 (and_13_out, decoder_1_out_3, Clock);
  and and_14 (and_14_out, decoder_1_out_7, Clock);
  and and_15 (and_15_out, decoder_1_out_11, Clock);
  and and_16 (and_16_out, decoder_1_out_15, Clock);
  General_Purpose_Register general_purpose_register_13 (
    .Clock(and_13_out), .Input(Data_Bus), .CLear_Store_Load(Control_Bus),
    .Output(general_purpose_register_13_output));
  General_Purpose_Register general_purpose_register_14 (
    .Clock(and_14_out), .Input(Data_Bus), .CLear_Store_Load(Control_Bus),
    .Output(general_purpose_register_14_output));
  General_Purpose_Register general_purpose_register_15 (
    .Clock(and_15_out), .Input(Data_Bus), .CLear_Store_Load(Control_Bus),
    .Output(general_purpose_register_15_output));
  General_Purpose_Register general_purpose_register_16 (
    .Clock(and_16_out), .Input(Data_Bus), .CLear_Store_Load(Control_Bus),
    .Output(general_purpose_register_16_output));
  Multiplexer #(.Selector_Bits(4), .Bits(4)) multiplexer_1 (
    .sel(Adress_Bus), .in_0(general_purpose_register_1_output), .in_1(general_purpose_register_5_output),
    .in_2(general_purpose_register_9_output), .in_3(general_purpose_register_13_output),
    .in_4(general_purpose_register_2_output), .in_5(general_purpose_register_6_output),
    .in_6(general_purpose_register_10_output), .in_7(general_purpose_register_14_output),
    .in_8(general_purpose_register_3_output), .in_9(general_purpose_register_7_output),
    .in_10(general_purpose_register_11_output), .in_11(general_purpose_register_15_output),
    .in_12(general_purpose_register_4_output), .in_13(general_purpose_register_8_output),
    .in_14(general_purpose_register_12_output), .in_15(general_purpose_register_16_output), .out(Data_Output));
endmodule
