// Digital circuit Program_Counter_register.dig as structural Verilog
module Program_Counter_register (
  input  Clock,
  input  [3:0] Input,
  input  [1:0] CLear_Store_Load_Increment,
  input  [3:0] Increment_Value,
  output [3:0] Output
);

  wire [3:0] add_1_s, multiplexer_1_out;

  Add #(.Bits(4)) add_1 (.a(Output), .b(Increment_Value), .c_i(1'b0), .s(add_1_s));  // open: c_o
  Multiplexer #(.Selector_Bits(2), .Bits(4)) multiplexer_1 (
    .sel(CLear_Store_Load_Increment), .in_0(4'b0000), .in_1(Input), .in_2(Output), .in_3(add_1_s),
    .out(multiplexer_1_out));
  D_FF d_ff_1 (.D(multiplexer_1_out[3]), .C(Clock), .Q(Output[3]));  // open: nQ
  D_FF d_ff_2 (.D(multiplexer_1_out[2]), .C(Clock), .Q(Output[2]));  // open: nQ
  D_FF d_ff_3 (.D(multiplexer_1_out[1]), .C(Clock), .Q(Output[1]));  // open: nQ
  D_FF d_ff_4 (.D(multiplexer_1_out[0]), .C(Clock), .Q(Output[0]));  // open: nQ

  // Notes on the sheet:
  //   CLear_Store_Load_Increment: 0 -> Clear to 0
  //   1-> Store Input Value
  //   2 ->Load
  //   3 -> Increment
  //   Increment_Value: Register increments by this value every clock tick, default 1
endmodule
