// Digital circuit Register_Files.dig as structural Verilog
module Register_Files (
  input  Clock,
  input  [1:0] Read_Register_1,
  input  [1:0] Read_Register_2,
  input  [7:0] Control_Signal,
  input  [1:0] Write_Register,
  input  [3:0] Write_Data,
  output [3:0] Read_Data_1,
  output [3:0] Read_Data_2
);

  wire [3:0] demultiplexer_1_out_0, demultiplexer_1_out_1, demultiplexer_1_out_2, demultiplexer_1_out_3,
       R0_output, R1_output, R2_output, R3_output;

  Demultiplexer #(.Selector_Bits(2), .Bits(4)) demultiplexer_1 (
    .sel(Write_Register), .in(Write_Data), .out_0(demultiplexer_1_out_0), .out_1(demultiplexer_1_out_1),
    .out_2(demultiplexer_1_out_2), .out_3(demultiplexer_1_out_3));
  General_Purpose_Register R0 (
    .Clock(Clock), .Input(demultiplexer_1_out_0), .CLear_Store_Load(Control_Signal[1:0]), .Output(R0_output));
  General_Purpose_Register R1 (
    .Clock(Clock), .Input(demultiplexer_1_out_1), .CLear_Store_Load(Control_Signal[3:2]), .Output(R1_output));
  General_Purpose_Register R2 (
    .Clock(Clock), .Input(demultiplexer_1_out_2), .CLear_Store_Load(Control_Signal[5:4]), .Output(R2_output));
  General_Purpose_Register R3 (
    .Clock(Clock), .Input(demultiplexer_1_out_3), .CLear_Store_Load(Control_Signal[7:6]), .Output(R3_output));
  Multiplexer #(.Selector_Bits(2), .Bits(4)) multiplexer_1 (
    .sel(Read_Register_1), .in_0(R0_output), .in_1(R1_output), .in_2(R2_output), .in_3(R3_output),
    .out(Read_Data_1));
  Multiplexer #(.Selector_Bits(2), .Bits(4)) multiplexer_2 (
    .sel(Read_Register_2), .in_0(R0_output), .in_1(R1_output), .in_2(R2_output), .in_3(R3_output),
    .out(Read_Data_2));

  // Notes on the sheet:
  //   Control_Signal: default 170
endmodule
