// Digital circuit 1BitAdder.dig as structural Verilog
module _1BitAdder (
  input  A,
  input  B,
  input  C_in,
  output Sum,
  output Carry_out
);

  wire and_1_out, and_2_out, xor_1_out;

  xor xor_1 (xor_1_out, A, B);
  and and_1 (and_1_out, A, B);
  xor xor_2 (Sum, xor_1_out, C_in);
  and and_2 (and_2_out, xor_1_out, C_in);
  or or_1 (Carry_out, and_1_out, and_2_out);
endmodule
