// Digital circuit hw1_full_adder.dig as structural Verilog
module hw1_full_adder (
  input  [3:0] A,
  input  [3:0] B,
  input  Carry_In,
  output [3:0] Sum,
  output Carry_out
);

  wire _1bitadder_2_y_2, _1bitadder_3_y_2, _1bitadder_4_y_2;

  _1BitAdder _1bitadder_1 (.A(A[3]), .B(B[3]), .C(_1bitadder_2_y_2), .Y(Sum[3]), .Y_2(Carry_out));
  _1BitAdder _1bitadder_2 (.A(A[2]), .B(B[2]), .C(_1bitadder_3_y_2), .Y(Sum[2]), .Y_2(_1bitadder_2_y_2));
  _1BitAdder _1bitadder_3 (.A(A[1]), .B(B[1]), .C(_1bitadder_4_y_2), .Y(Sum[1]), .Y_2(_1bitadder_3_y_2));
  _1BitAdder _1bitadder_4 (.A(A[0]), .B(B[0]), .C(Carry_In), .Y(Sum[0]), .Y_2(_1bitadder_4_y_2));
endmodule
