// Digital circuit hw1_multiplier.dig as structural Verilog
module hw1_multiplier (
  input  [1:0] A,
  input  [1:0] B,
  output [3:0] P
);

  wire and_2_out, and_3_out, and_4_out, and_5_out, and_6_out, and_7_out, not_1_out, not_2_out, not_3_out,
       not_4_out;

  not not_1 (not_1_out, A[0]);
  not not_2 (not_2_out, B[0]);
  not not_3 (not_3_out, A[1]);
  not not_4 (not_4_out, B[1]);
  and and_1 (P[3], A[0], A[1], B[0], B[1]);
  and and_2 (and_2_out, A[1], B[1], not_2_out);
  and and_3 (and_3_out, A[1], B[1], not_1_out);
  and and_4 (and_4_out, A[0], B[1], not_3_out);
  and and_5 (and_5_out, A[0], B[1], not_2_out);
  and and_6 (and_6_out, A[1], B[0], not_4_out);
  and and_7 (and_7_out, A[1], B[0], not_1_out);
  and and_8 (P[0], B[0], A[0]);
  or or_1 (P[2], and_2_out, and_3_out);
  or or_2 (P[1], and_4_out, and_5_out, and_6_out, and_7_out);
endmodule
