// Digital circuit HW2Circuit#9.dig as structural Verilog
module HW2Circuit_9 (
  input  I,
  input  clk,
  output Output,
  output [1:0] State_temp
);

  wire and_1_out, and_2_out, and_3_out, and_4_out, and_5_out, not_1_out, or_1_out, or_2_out, S0_nq, S1_nq;

  not not_1 (not_1_out, I);
  and and_1 (and_1_out, S1_nq, State_temp[0], I);
  and and_2 (and_2_out, State_temp[1], S0_nq, not_1_out);
  and and_3 (and_3_out, S0_nq, I);
  and and_4 (and_4_out, State_temp[1], I);
  and and_5 (and_5_out, State_temp[1], S0_nq);
  or or_1 (or_1_out, and_1_out, and_2_out);
  or or_2 (or_2_out, and_3_out, and_4_out, and_5_out);
  D_FF S1 (.D(or_1_out), .C(clk), .Q(State_temp[1]), .nQ(S1_nq));
  D_FF S0 (.D(or_2_out), .C(clk), .Q(State_temp[0]), .nQ(S0_nq));
  and and_6 (Output, State_temp[1], S0_nq, not_1_out);
endmodule
