// Digital circuit Oct012025_Participation_Circuit.dig as structural Verilog
module Oct012025_Participation_Circuit (
  input  i,
  input  clk,
  output O,
  output [1:0] States__S_1__S_0
);

  wire and_1_out, and_2_out, and_3_out, and_4_out, and_5_out, D_S0_nq, D_S1_nq, not_1_out, or_1_out, or_2_out;

  not not_1 (not_1_out, i);
  and and_1 (and_1_out, States__S_1__S_0[0], not_1_out);
  and and_2 (and_2_out, D_S0_nq, i);
  and and_3 (and_3_out, States__S_1__S_0[1], not_1_out);
  and and_4 (and_4_out, States__S_1__S_0[1], D_S0_nq);
  and and_5 (and_5_out, i, States__S_1__S_0[0], D_S1_nq);
  or or_1 (or_1_out, and_1_out, and_2_out);
  or or_2 (or_2_out, and_3_out, and_4_out, and_5_out);
  D_FF D_S1 (.D(or_2_out), .C(clk), .Q(States__S_1__S_0[1]), .nQ(D_S1_nq));
  D_FF D_S0 (.D(or_1_out), .C(clk), .Q(States__S_1__S_0[0]), .nQ(D_S0_nq));
  and and_6 (O, i, States__S_1__S_0[1], States__S_1__S_0[0]);
endmodule
