// Digital circuit Oct272025_Participation_AdderSubtractor.dig as structural Verilog
module Oct272025_Participation_AdderSubtractor (
  input  [3:0] A,
  input  [3:0] B,
  input  Add_Subtract,
  output [3:0] Sum,
  output Carry_Out
);

  wire _1bitadder_2_carry_out, _1bitadder_3_carry_out, _1bitadder_4_carry_out, xor_1_out, xor_2_out,
       xor_3_out, xor_4_out;

  xor xor_1 (xor_1_out, B[0], Add_Subtract);
  xor xor_2 (xor_2_out, B[1], Add_Subtract);
  xor xor_3 (xor_3_out, B[2], Add_Subtract);
  xor xor_4 (xor_4_out, B[3], Add_Subtract);
  _1BitAdder _1bitadder_1 (.A(A[3]), .B(xor_4_out), .C_in(_1bitadder_2_carry_out), .Sum(Sum[3]), .Carry_out(Carry_Out));
  _1BitAdder _1bitadder_2 (
    .A(A[2]), .B(xor_3_out), .C_in(_1bitadder_3_carry_out), .Sum(Sum[2]), .Carry_out(_1bitadder_2_carry_out));
  _1BitAdder _1bitadder_3 (
    .A(A[1]), .B(xor_2_out), .C_in(_1bitadder_4_carry_out), .Sum(Sum[1]), .Carry_out(_1bitadder_3_carry_out));
  _1BitAdder _1bitadder_4 (
    .A(A[0]), .B(xor_1_out), .C_in(Add_Subtract), .Sum(Sum[0]), .Carry_out(_1bitadder_4_carry_out));

  // Notes on the sheet:
  //   Add_Subtract: 0 = Add
  //   1 = Subtract
endmodule
