// Digital circuit Oct292025_Participation_FullALU.dig as structural Verilog
module Oct292025_Participation_FullALU (
  input  [3:0] A,
  input  [3:0] B,
  input  [1:0] S_1_S_0,
  input  Carry_In,
  output [3:0] D,
  output Carry_Out
);

  wire [3:0] multiplexer_1_out, not_1_out, not_2_out;

  assign not_1_out = ~B;  // Not not_1, 4 bits wide
  assign not_2_out = ~4'b0000;  // Not not_2, 4 bits wide
  Multiplexer #(.Selector_Bits(2), .Bits(4)) multiplexer_1 (
    .sel(S_1_S_0), .in_0(B), .in_1(not_1_out), .in_2(4'b0000), .in_3(not_2_out), .out(multiplexer_1_out));
  hw1_full_adder hw1_full_adder_1 (.A(A), .B(multiplexer_1_out), .Carry_In(Carry_In), .Sum(D), .Carry_out(Carry_Out));

  // Notes on the sheet:
  //   S_1_S_0: This selector pin will determine which pair 
  //   of operations the circuit will complete. The 
  //   value of the carry in will split the function to
  //   lower so that it can complete one of the given 
  //   functions:
  //   00: Add/Add with Carry
  //   01: Subtract with Borrow/Subtract
  //   10: Transfer A/Increment A
  //   11: Decrement A/Transfer A
  //   Carry_In: 0: first option named in selector bit
  //   1: second option named in selector bit
endmodule
