// Digital circuit SR_FlipFlop.dig as structural Verilog
module SR_FlipFlop (
  input  S,
  input  R,
  input  clk,
  output Q,
  output Q_2
);

  wire nand_1_out, nand_2_out;

  nand nand_1 (nand_1_out, S, clk);
  nand nand_2 (nand_2_out, clk, R);
  nand nand_3 (Q, nand_1_out, Q_2);
  nand nand_4 (Q_2, Q, nand_2_out);
endmodule
