// Digital circuit demultiplexer_basic.dig as structural Verilog
module demultiplexer_basic (
  input  S1,
  input  S0,
  input  Data,
  output Output_3,
  output Output_2,
  output Output_1,
  output Output_0
);

  wire not_1_out, not_2_out;

  not not_1 (not_1_out, S1);
  not not_2 (not_2_out, S0);
  and and_1 (Output_0, not_1_out, not_2_out, Data);
  and and_2 (Output_1, S1, not_2_out, Data);
  and and_3 (Output_2, not_1_out, S0, Data);
  and and_4 (Output_3, S1, S0, Data);
endmodule
