// Digital circuit fullCircuit_Oct82025.dig as structural Verilog
module fullCircuit_Oct82025 (
  input  if_mem_ready,
  input  id_done,
  input  is_Rtype,
  input  clk
);

  wire and_1_out, and_2_out, D_0_q, D_1_q;

  and and_1 (and_1_out, D_0_q, if_mem_ready);
  and and_2 (and_2_out, D_1_q, id_done, is_Rtype);
  D_FF D_0 (.C(clk), .Q(D_0_q));  // open: D, nQ
  D_FF D_1 (.D(and_1_out), .C(clk), .Q(D_1_q));  // open: nQ
  D_FF D_2 (.D(and_2_out), .C(clk));  // open: Q, nQ
  D_FF d_ff_1 ();  // open: D, C, Q, nQ
endmodule
