// Digital circuit placeholder.dig as structural Verilog
module placeholder (
  input  Clock,
  input  [1:0] InstructionMemory_ctrl,
  input  [1:0] InstructionPointer_ctrl,
  input  [3:0] InstructionMemory_dataInput,
  output [3:0] out_5
);

  wire [3:0] Instruction_Memory_data_output, program_counter_register_1_output;

  Program_Counter_register program_counter_register_1 (
    .Clock(Clock), .Input(4'b0000), .CLear_Store_Load_Increment(InstructionPointer_ctrl),
    .Increment_Value(4'b0001), .Output(program_counter_register_1_output));
  DRAM Instruction_Memory (
    .Clock(Clock), .Adress_Bus(program_counter_register_1_output), .Control_Bus(InstructionMemory_ctrl),
    .Data_Bus(InstructionMemory_dataInput), .Data_Output(Instruction_Memory_data_output));
  Instruction_Register instruction_register_1 (
    .Clock(Clock), .Input(Instruction_Memory_data_output), .CLear_Store_Load(2'b01), .Output(out_5));
endmodule
